// Logisim project conversor-7segmentos.circ as structural Verilog: 1 circuit, main circuit main
module main (
  input  in_1,
  input  in_2,
  input  in_3,
  output out_4,
  output out_5,
  output out_6,
  output out_7,
  output out_8,
  output out_9,
  output out_10
);

  wire and_1_out, and_2_out, and_3_out, and_4_out, and_5_out, and_6_out, and_7_out, and_8_out, and_9_out,
       nor_1_out, not_1_out, not_2_out, not_3_out, not_4_out, not_5_out, not_6_out, not_7_out, not_8_out,
       undriven, undriven_2, undriven_3, undriven_4, undriven_5, undriven_6, undriven_7, xnor_1_out,
       xnor_2_out, xnor_3_out;

  not not_1 (not_1_out, in_3);
  not not_2 (not_2_out, in_1);
  not not_3 (not_3_out, in_2);
  not not_4 (not_4_out, in_3);
  not not_5 (not_5_out, in_1);
  not not_6 (not_6_out, in_3);
  not not_7 (not_7_out, in_1);
  and and_1 (and_1_out, not_1_out, not_2_out);
  and and_2 (and_2_out, in_1, not_3_out, in_3);
  and and_3 (and_3_out, not_3_out, in_1);
  and and_4 (and_4_out, not_3_out, not_4_out);
  and and_5 (and_5_out, not_4_out, in_1);
  xnor xnor_1 (xnor_1_out, in_2, not_5_out);
  and and_6 (and_6_out, in_1, not_6_out);
  xnor xnor_2 (xnor_2_out, in_3, in_1);
  xnor xnor_3 (xnor_3_out, in_3, in_2);
  not not_8 (not_8_out, in_2);
  and and_7 (and_7_out, not_2_out, in_2);
  and and_8 (and_8_out, in_2, not_1_out);
  nor nor_1 (nor_1_out, in_1, in_3);
  and and_9 (and_9_out, in_2, not_1_out);
  or or_1 (out_4, xnor_2_out, in_2);
  or or_2 (out_5, xnor_3_out, not_7_out);
  or or_3 (out_6, in_3, not_8_out, in_1);
  or or_4 (out_7, and_1_out, and_7_out, and_8_out, and_2_out);
  or or_5 (out_8, nor_1_out, and_9_out);
  or or_6 (out_9, and_3_out, and_4_out, and_5_out);
  or or_7 (out_10, xnor_1_out, and_6_out);
  _7_Segment_Display u_7_segment_display_1 (
    .g(undriven_4), .f(undriven_3), .a(undriven_2), .b(undriven), .e(undriven_5), .d(undriven_5),
    .c(undriven_6), .dp(undriven_7));
endmodule
