// Logisim project somador-3bits.circ as structural Verilog: 1 circuit, main circuit main
module main (
  input  b0,
  input  a0,
  input  b1,
  input  a1,
  input  b2,
  input  a2,
  output s0,
  output s1,
  output s2,
  output CARRRY
);

  wire and_1_out, and_2_out, and_3_out, and_4_out, and_5_out, and_6_out, xor_1_out, xor_2_out, xor_3_out,
       xor_7_out, xor_8_out;

  xor xor_1 (xor_1_out, b0, a0);
  xor xor_2 (xor_2_out, a1, b1);
  and and_1 (and_1_out, xor_1_out, 1'b0);
  and and_2 (and_2_out, a0, b0);
  and and_3 (and_3_out, xor_2_out, xor_7_out);
  and and_4 (and_4_out, b1, a1);
  xor xor_3 (xor_3_out, a2, b2);
  xor xor_4 (s0, xor_1_out, 1'b0);
  xor xor_5 (s1, xor_2_out, xor_7_out);
  xor xor_6 (s2, xor_3_out, xor_8_out);
  and and_5 (and_5_out, xor_3_out, xor_8_out);
  and and_6 (and_6_out, b2, a2);
  xor xor_7 (xor_7_out, and_1_out, and_2_out);
  xor xor_8 (xor_8_out, and_3_out, and_4_out);
  xor xor_9 (CARRRY, and_5_out, and_6_out);
endmodule
