// Logisim project tarsila_projeto_aulas8_9.circ as structural Verilog: 1 circuit, main circuit main
module main (
  input  in_1,
  input  in_2,
  input  in_3,
  input  in_4,
  input  in_5,
  input  in_6
);

  wire clock_1_out, main_1_p7, main_1_p8, main_1_p9, main_2_out_5, main_2_out_6, main_2_out_7, main_3_out_4,
       main_3_out_5, main_3_out_6, main_3_out_7, main_3_out_8, main_3_out_9, main_3_out_10;

  Clock clock_1 (.out(clock_1_out));
  // somador_3bits_main main_1: pin names not known; wires that end beside it: in_1, in_2, in_3, in_4, in_5, in_6, main_1_p7, main_1_p8, main_1_p9
  registrador_3bits_main main_2 (
    .in_1(clock_1_out), .in_2(main_1_p7), .in_3(main_1_p8), .in_4(main_1_p9), .out_5(main_2_out_5),
    .out_6(main_2_out_6), .out_7(main_2_out_7));
  conversor_7segmentos_main main_3 (
    .out_4(main_3_out_4), .out_5(main_3_out_5), .out_6(main_3_out_6), .out_7(main_3_out_7),
    .out_8(main_3_out_8), .out_9(main_3_out_9), .out_10(main_3_out_10), .in_1(main_2_out_5),
    .in_2(main_2_out_6), .in_3(main_2_out_7));
  _7_Segment_Display u_7_segment_display_1 (
    .g(main_3_out_10), .f(main_3_out_9), .a(main_3_out_4), .b(main_3_out_5), .e(main_3_out_8),
    .d(main_3_out_7), .c(main_3_out_6));  // open: dp
endmodule
